// Logisim project V1 - Projeto PPT.circ as structural Verilog: 1 circuit, main circuit main
module main (
);

  wire Papel_out, Pedra_out, Porta_A_out, Tesoura_out;

  Button Pedra (.out(Pedra_out));
  Button Papel (.out(Papel_out));
  Button Tesoura (.out(Tesoura_out));
  and Porta_A (Porta_A_out, Pedra_out, Papel_out, Tesoura_out);
  TTY tty_1 (.we(Porta_A_out));  // open: data, clk, clr
  Random #(.seed(3)) \Gerador_Aleatório  ();  // open: clk, next, out, clr
endmodule
