// Logisim project V2 - Projeto PSR.circ as structural Verilog: 1 circuit, main circuit main
module main (
  input  P1,
  input  S1,
  input  R1,
  input  P2,
  input  S2,
  input  R2,
  output out_7,
  output EMPATE,
  output out_9
);

  and and_1 (out_7, P1, P2);
  and and_2 (EMPATE, P1, S2);
  and and_3 (out_9, P1, R2);
  and and_4 (out_9, S1, P2);
  and and_5 (EMPATE, S1, S2);
  and and_6 (out_7, S1, R2);
  and and_7 (out_7, R1, P2);
  and and_8 (out_9, R1, S2);
  and and_9 (EMPATE, R1, R2);

  // Notes on the sheet:
  //   VITORIA JOGADOR 1
  //   VITORIA JOGADOR 2
endmodule
