// Logisim project V4 - Projeto RPS Dois Botoes.circ as structural Verilog: 1 circuit, main circuit main
module main (
  input  P1,
  input  S1,
  input  R1,
  input  P2,
  input  S2,
  input  R2,
  output out_7,
  output out_8,
  output out_9
);

  wire and_1_out, and_2_out, and_3_out, and_4_out, and_5_out, and_6_out, and_7_out, and_8_out, and_9_out,
       and_10_out, and_11_out, and_12_out, and_13_out, and_14_out, and_15_out, not_1_out, not_2_out,
       not_3_out, not_4_out, not_5_out, not_6_out, or_1_out, or_2_out, or_3_out, or_4_out, or_5_out, or_6_out;

  not not_1 (not_1_out, or_1_out);
  or or_1 (or_1_out, S1, R1);
  or or_2 (or_2_out, P1, R1);
  or or_3 (or_3_out, P1, S1);
  not not_2 (not_2_out, or_4_out);
  or or_4 (or_4_out, S2, R2);
  and and_1 (and_1_out, P1, not_1_out);
  and and_2 (and_2_out, S1, not_3_out);
  not not_3 (not_3_out, or_2_out);
  and and_3 (and_3_out, R1, not_4_out);
  not not_4 (not_4_out, or_3_out);
  and and_4 (and_4_out, P2, not_2_out);
  and and_5 (and_5_out, S2, not_5_out);
  not not_5 (not_5_out, or_5_out);
  or or_5 (or_5_out, P2, R2);
  not not_6 (not_6_out, or_6_out);
  or or_6 (or_6_out, P2, S2);
  and and_6 (and_6_out, R2, not_6_out);
  and and_7 (and_7_out, and_1_out, and_4_out);
  and and_8 (and_8_out, and_1_out, and_5_out);
  and and_9 (and_9_out, and_1_out, and_6_out);
  and and_10 (and_10_out, and_2_out, and_4_out);
  and and_11 (and_11_out, and_2_out, and_5_out);
  and and_12 (and_12_out, and_2_out, and_6_out);
  and and_13 (and_13_out, and_3_out, and_4_out);
  and and_14 (and_14_out, and_3_out, and_5_out);
  and and_15 (and_15_out, and_3_out, and_6_out);
  or or_7 (out_7, and_9_out, and_10_out, and_14_out);
  or or_8 (out_8, and_7_out, and_11_out, and_15_out);
  or or_9 (out_9, and_8_out, and_12_out, and_13_out);
  LED led_1 (.in(out_7));
  LED led_2 (.in(out_8));
  LED led_3 (.in(out_9));

  // Notes on the sheet:
  //   VITORIA JOGADOR 1
  //   EMPATE
  //   VITORIA JOGADOR 2
endmodule
