// Logisim project V5 - Projeto RPS Resumido.circ as structural Verilog: 1 circuit, main circuit main
module main (
  input  P1,
  input  S1,
  input  R1,
  input  P2,
  input  S2,
  input  R2,
  output x,
  output y,
  output z
);

  wire and_1_out, and_2_out, and_3_out, and_4_out, and_5_out, and_6_out, and_7_out, and_8_out, and_9_out,
       not_1_out, not_2_out, not_3_out, not_4_out, not_5_out, not_6_out, not_7_out, not_8_out, not_9_out,
       not_10_out, not_11_out, not_12_out, not_13_out, not_14_out, not_15_out, not_16_out, not_17_out,
       not_18_out, not_19_out, not_20_out, not_21_out, not_22_out, not_23_out, not_24_out, not_25_out,
       not_26_out, not_27_out, not_28_out, not_29_out, not_30_out, not_31_out, not_32_out, not_33_out,
       not_34_out, not_35_out, not_36_out;

  not not_1 (not_1_out, P1);
  not not_2 (not_2_out, S1);
  not not_3 (not_3_out, P2);
  not not_4 (not_4_out, R2);
  not not_5 (not_5_out, P1);
  not not_6 (not_6_out, R1);
  not not_7 (not_7_out, S2);
  not not_8 (not_8_out, R2);
  not not_9 (not_9_out, S1);
  not not_10 (not_10_out, R1);
  not not_11 (not_11_out, P2);
  not not_12 (not_12_out, S2);
  not not_13 (not_13_out, P1);
  not not_14 (not_14_out, S1);
  not not_15 (not_15_out, P2);
  not not_16 (not_16_out, S2);
  not not_17 (not_17_out, P1);
  not not_18 (not_18_out, R1);
  not not_19 (not_19_out, P2);
  not not_20 (not_20_out, R2);
  not not_21 (not_21_out, S1);
  not not_22 (not_22_out, R1);
  not not_23 (not_23_out, S2);
  not not_24 (not_24_out, R2);
  not not_25 (not_25_out, P1);
  not not_26 (not_26_out, S1);
  not not_27 (not_27_out, S2);
  not not_28 (not_28_out, R2);
  not not_29 (not_29_out, P1);
  not not_30 (not_30_out, R1);
  not not_31 (not_31_out, P2);
  not not_32 (not_32_out, S2);
  not not_33 (not_33_out, S1);
  not not_34 (not_34_out, R1);
  not not_35 (not_35_out, P2);
  not not_36 (not_36_out, R2);
  and and_1 (and_1_out, not_1_out, not_2_out, R1, not_3_out, S2, not_4_out);
  and and_2 (and_2_out, not_5_out, S1, not_6_out, P2, not_7_out, not_8_out);
  and and_3 (and_3_out, P1, not_9_out, not_10_out, not_11_out, not_12_out, R2);
  and and_4 (and_4_out, not_13_out, not_14_out, R1, not_15_out, not_16_out, R2);
  and and_5 (and_5_out, not_17_out, S1, not_18_out, not_19_out, S2, not_20_out);
  and and_6 (and_6_out, P1, not_21_out, not_22_out, P2, not_23_out, not_24_out);
  and and_7 (and_7_out, not_25_out, not_26_out, R1, P2, not_27_out, not_28_out);
  and and_8 (and_8_out, not_29_out, S1, not_30_out, not_31_out, not_32_out, R2);
  and and_9 (and_9_out, P1, not_33_out, not_34_out, not_35_out, S2, not_36_out);
  or or_1 (x, and_1_out, and_2_out, and_3_out);
  or or_2 (y, and_4_out, and_5_out, and_6_out);
  or or_3 (z, and_7_out, and_8_out, and_9_out);
endmodule
