// Logisim project V6 - Projeto PPT FINALIZADO.circ as structural Verilog: 1 circuit, main circuit main
module main (
  input  J1PAPEL,
  input  J1TESOURA,
  input  J1PEDRA,
  input  J2PAPEL,
  input  J2TESOURA,
  input  J2PEDRA,
  output ERRO_J1,
  output J1,
  output EMAPTE,
  output J2,
  output ERRO_J2
);

  wire and_1_out, and_2_out, and_3_out, and_4_out, and_5_out, and_6_out, and_7_out, and_8_out, and_9_out,
       and_10_out, and_11_out, and_12_out, and_13_out, and_14_out, and_15_out, and_16_out, and_17_out,
       and_18_out, and_19_out, and_20_out, and_21_out, not_1_out, not_2_out, not_3_out, not_4_out, not_5_out,
       not_6_out, or_1_out, or_2_out, or_3_out, or_4_out, or_5_out, or_6_out;

  not not_1 (not_1_out, or_1_out);
  or or_1 (or_1_out, J1TESOURA, J1PEDRA);
  or or_2 (or_2_out, J1PAPEL, J1PEDRA);
  or or_3 (or_3_out, J1PAPEL, J1TESOURA);
  not not_2 (not_2_out, or_4_out);
  or or_4 (or_4_out, J2TESOURA, J2PEDRA);
  not not_3 (not_3_out, or_5_out);
  or or_5 (or_5_out, J2PAPEL, J2PEDRA);
  or or_6 (or_6_out, J2PAPEL, J2TESOURA);
  and and_1 (and_1_out, J1PAPEL, not_1_out);
  and and_2 (and_2_out, J1TESOURA, not_4_out);
  not not_4 (not_4_out, or_2_out);
  and and_3 (and_3_out, J1PEDRA, not_5_out);
  not not_5 (not_5_out, or_3_out);
  and and_4 (and_4_out, J2PAPEL, not_2_out);
  and and_5 (and_5_out, J2TESOURA, not_3_out);
  not not_6 (not_6_out, or_6_out);
  and and_6 (and_6_out, J2PEDRA, not_6_out);
  and and_7 (and_7_out, J1PAPEL, J1TESOURA);
  and and_8 (and_8_out, J1PAPEL, J1PEDRA);
  and and_9 (and_9_out, J1TESOURA, J1PEDRA);
  and and_10 (and_10_out, and_1_out, and_4_out);
  and and_11 (and_11_out, and_1_out, and_5_out);
  and and_12 (and_12_out, and_1_out, and_6_out);
  and and_13 (and_13_out, and_2_out, and_4_out);
  and and_14 (and_14_out, and_2_out, and_5_out);
  and and_15 (and_15_out, and_2_out, and_6_out);
  and and_16 (and_16_out, and_3_out, and_4_out);
  and and_17 (and_17_out, and_3_out, and_5_out);
  and and_18 (and_18_out, and_3_out, and_6_out);
  or or_7 (ERRO_J1, and_7_out, and_8_out, and_9_out);
  and and_19 (and_19_out, J2PAPEL, J2TESOURA);
  and and_20 (and_20_out, J2PAPEL, J2PEDRA);
  and and_21 (and_21_out, J2TESOURA, J2PEDRA);
  or or_8 (ERRO_J2, and_19_out, and_20_out, and_21_out);
  or or_9 (J1, and_12_out, and_13_out, and_17_out);
  or or_10 (EMAPTE, and_10_out, and_14_out, and_18_out);
  or or_11 (J2, and_11_out, and_15_out, and_16_out);
  LED led_1 (.in(J1));
  LED led_2 (.in(EMAPTE));
  LED led_3 (.in(J2));

  // Notes on the sheet:
  //   VITORIA JOGADOR 1
  //   VITORIA JOGADOR 2
endmodule
