// Logisim project ATV 2 - LeonardoMiguelSantos.circ as structural Verilog: 1 circuit, main circuit main
module main (
  input  J1PAPEL,
  input  J1TESOURA,
  input  J1PEDRA,
  input  J2PAPEL,
  input  J2TESOURA,
  input  J2PEDRA,
  output ERRO_J1,
  output J1,
  output VENCEDOR_J1,
  output EMAPTE,
  output VENCEDOR_J2,
  output J2,
  output ERRO_J2
);

  wire and_1_out, and_2_out, and_3_out, and_4_out, and_5_out, and_6_out, and_7_out, and_8_out, and_9_out,
       and_10_out, and_11_out, and_12_out, and_13_out, and_14_out, and_15_out, and_16_out, and_17_out,
       and_18_out, and_19_out, and_20_out, and_21_out, and_22_out, and_23_out, and_24_out, and_25_out,
       and_26_out, and_27_out, d_ff_1_q, d_ff_2_q, d_ff_3_q, d_ff_4_q, d_ff_5_q, d_ff_6_q, Jogar_out,
       JOGO_DECIDIDO_out, not_1_out, not_2_out, not_3_out, not_4_out, not_5_out, not_6_out, not_7_out,
       or_1_out, or_2_out, or_3_out, or_4_out, or_5_out, or_6_out, Reset_out;

  or JOGO_DECIDIDO (JOGO_DECIDIDO_out, VENCEDOR_J1, VENCEDOR_J2);
  LED led_1 (.in(VENCEDOR_J1));
  not not_1 (not_1_out, JOGO_DECIDIDO_out);
  LED led_2 (.in(VENCEDOR_J2));
  and and_1 (and_1_out, J1PAPEL, not_1_out);
  and and_2 (and_2_out, J1TESOURA, not_1_out);
  and and_3 (and_3_out, J1PEDRA, not_1_out);
  Button Jogar (.out(Jogar_out));
  Button Reset (.out(Reset_out));
  and and_4 (and_4_out, J2PAPEL, not_1_out);
  and and_5 (and_5_out, J2TESOURA, not_1_out);
  and and_6 (and_6_out, J2PEDRA, not_1_out);
  D_Flip_Flop d_ff_1 (.clk(Jogar_out), .D(and_1_out), .Q(d_ff_1_q), .reset(Reset_out));  // open: Qn, preset, en
  D_Flip_Flop d_ff_2 (.clk(Jogar_out), .D(and_2_out), .Q(d_ff_2_q), .reset(Reset_out));  // open: Qn, preset, en
  D_Flip_Flop d_ff_3 (.clk(Jogar_out), .D(and_3_out), .Q(d_ff_3_q), .reset(Reset_out));  // open: Qn, preset, en
  D_Flip_Flop d_ff_4 (.clk(Jogar_out), .D(and_4_out), .Q(d_ff_4_q), .reset(Reset_out));  // open: Qn, preset, en
  D_Flip_Flop d_ff_5 (.clk(Jogar_out), .D(and_5_out), .Q(d_ff_5_q), .reset(Reset_out));  // open: Qn, preset, en
  D_Flip_Flop d_ff_6 (.clk(Jogar_out), .D(and_6_out), .Q(d_ff_6_q), .reset(Reset_out));  // open: Qn, preset, en
  not not_2 (not_2_out, or_1_out);
  or or_1 (or_1_out, d_ff_2_q, d_ff_3_q);
  or or_2 (or_2_out, d_ff_1_q, d_ff_3_q);
  or or_3 (or_3_out, d_ff_1_q, d_ff_2_q);
  and and_7 (and_7_out, d_ff_1_q, not_2_out);
  not not_3 (not_3_out, or_2_out);
  not not_4 (not_4_out, or_3_out);
  and and_8 (and_8_out, d_ff_4_q, not_5_out);
  not not_5 (not_5_out, or_4_out);
  or or_4 (or_4_out, d_ff_5_q, d_ff_6_q);
  and and_9 (and_9_out, d_ff_5_q, not_6_out);
  not not_6 (not_6_out, or_5_out);
  or or_5 (or_5_out, d_ff_4_q, d_ff_6_q);
  not not_7 (not_7_out, or_6_out);
  or or_6 (or_6_out, d_ff_4_q, d_ff_5_q);
  and and_10 (and_10_out, d_ff_2_q, not_3_out);
  and and_11 (and_11_out, d_ff_3_q, not_4_out);
  and and_12 (and_12_out, d_ff_6_q, not_7_out);
  and and_13 (and_13_out, d_ff_1_q, d_ff_2_q);
  and and_14 (and_14_out, d_ff_1_q, d_ff_3_q);
  and and_15 (and_15_out, d_ff_2_q, d_ff_3_q);
  and and_16 (and_16_out, and_7_out, and_8_out);
  and and_17 (and_17_out, and_7_out, and_9_out);
  and and_18 (and_18_out, and_7_out, and_12_out);
  and and_19 (and_19_out, and_10_out, and_8_out);
  and and_20 (and_20_out, and_10_out, and_9_out);
  and and_21 (and_21_out, and_10_out, and_12_out);
  and and_22 (and_22_out, and_11_out, and_8_out);
  and and_23 (and_23_out, and_11_out, and_9_out);
  and and_24 (and_24_out, and_11_out, and_12_out);
  and and_25 (and_25_out, d_ff_4_q, d_ff_5_q);
  and and_26 (and_26_out, d_ff_4_q, d_ff_6_q);
  and and_27 (and_27_out, d_ff_5_q, d_ff_6_q);
  or or_7 (ERRO_J1, and_13_out, and_14_out, and_15_out);
  or or_8 (ERRO_J2, and_25_out, and_26_out, and_27_out);
  or or_9 (J1, and_18_out, and_19_out, and_23_out);
  or or_10 (EMAPTE, and_16_out, and_20_out, and_24_out);
  or or_11 (J2, and_17_out, and_21_out, and_22_out);
  LED led_3 (.in(J1));
  Counter #(.width(2), .max('h3), .ongoal("stay")) \PONTUAÇÃO_J1  (
    .carry(VENCEDOR_J1), .clk(J1), .clr(Reset_out));  // open: load, D, count, Q
  LED led_4 (.in(EMAPTE));
  Counter #(.width(2), .max('h3), .ongoal("stay")) \PONTUAÇÃO_J2  (
    .carry(VENCEDOR_J2), .clk(J2), .clr(Reset_out));  // open: load, D, count, Q
  LED led_5 (.in(J2));

  // Notes on the sheet:
  //   RODADA JOGADOR 1
  //   RODADA JOGADOR 2
endmodule
