// Logisim project Projeto RPS Funcionando.circ as structural Verilog: 1 circuit, main circuit main
module main (
  input  P1,
  input  S1,
  input  R1,
  input  P2,
  input  S2,
  input  R2
);

  wire and_1_out, and_2_out, and_3_out, and_4_out, and_5_out, and_6_out, and_7_out, and_8_out, and_9_out,
       or_1_out, or_2_out, or_3_out;

  and and_1 (and_1_out, P1, P2);
  and and_2 (and_2_out, P1, S2);
  and and_3 (and_3_out, P1, R2);
  and and_4 (and_4_out, S1, P2);
  and and_5 (and_5_out, S1, S2);
  and and_6 (and_6_out, S1, R2);
  and and_7 (and_7_out, R1, P2);
  and and_8 (and_8_out, R1, S2);
  and and_9 (and_9_out, R1, R2);
  or or_1 (or_1_out, and_3_out, and_4_out, and_8_out);
  or or_2 (or_2_out, and_1_out, and_5_out, and_9_out);
  or or_3 (or_3_out, and_2_out, and_6_out, and_7_out);
  LED led_1 (.in(or_1_out));
  LED led_2 (.in(or_2_out));
  LED led_3 (.in(or_3_out));

  // Notes on the sheet:
  //   VITORIA JOGADOR 1
  //   EMPATE
  //   VITORIA JOGADOR 2
endmodule
