// Logisim project At2.circ as structural Verilog: 1 circuit, main circuit main
module main (
  input  S,
  input  R,
  output Q,
  output Q_2
);

  nor nor_1 (Q, S, Q_2);
  nor nor_2 (Q_2, Q, R);

  // Notes on the sheet:
  //   Célula de Armazenamento por Retroalimentação/Feedback
  //   - Memoriza qual a última combinação de valores lógicas impressas no sistema
  //   - Q e Q| devem obrigatóriamente serem opostos, nunca podem ser iguais em valor
endmodule
