// Logisim project Controle Elevador.circ as structural Verilog: 1 circuit, main circuit main
module main (
  input  Elevador,
  input  Andar,
  input  Timer_Elevador,
  input  Sensor,
  output PORTA_FECHA
);

  wire and_1_out, not_1_out, or_1_out;

  Counter Timer_10s ();  // open: load, D, count, Q, carry, clk, clr
  not not_1 (not_1_out, Sensor);
  or or_1 (or_1_out, Elevador, Andar);
  and and_1 (and_1_out, Timer_Elevador, not_1_out);
  and and_2 (PORTA_FECHA, or_1_out, and_1_out);

  // Notes on the sheet:
  //   CONTROLE ELEVADOR
  //   CONTROLE PORTA
endmodule
