// Logisim project Projeto LGR.circ as structural Verilog: 1 circuit, main circuit main
module main (
  input  Lobo,
  input  Gato,
  input  Rato,
  output out_4
);

  wire and_1_out, and_2_out;

  and and_1 (and_1_out, Lobo, Gato);
  and and_2 (and_2_out, Gato, Rato);
  or or_1 (out_4, and_1_out, and_2_out);
  LED led_1 (.in(out_4));
endmodule
